# Fritzing sketch schematic (saved by Fritzing 0.9.6b)
breadboards: 1

parts:
  Part1 = Arduino Uno (Rev3) - ICSP
  DFRobot_DFPlayer_Mini1 = DFRobot DFPlayer Mini [part_number=DFR0299]
  HC-SR04_Sensor_1 = HC-SR04 Ultrasonic Distance Sensor
  LED1 = LED - 5mm [color="White (8000K)" current=0.030 package="5 mm [THT]"]
  R1 = Resistor [tolerance=±5% power=0.25 resistance=1000 package=THT]
  U1 = POT [package=pot_mammoth]
  SP1 = SPEAKER [package=pcb_mount_speaker]
  LED2 = LED - 5mm [color="Yellow (585nm)" current=0.030 package="5 mm [THT]"]
  R2 = Resistor [tolerance=±5% power=0.25 resistance=1000 package=THT]
  R3 = Resistor [tolerance=±5% power=0.25 resistance=1000 package=THT]
  LED3 = LED - 5mm [color="Green (555nm)" current=0.030 package="5 mm [THT]"]
  LED4 = LED - 5mm [color="Red (633nm)" current=0.030 package="5 mm [THT]"]
  R4 = Resistor [tolerance=±5% power=0.25 resistance=1000 package=THT]
  R5 = Resistor [tolerance=±5% power=0.25 resistance=1000 package=THT]

nets:
  N1: Part1.A0, U1.A
  N2: Part1.D10_PWM/SS, DFRobot_DFPlayer_Mini1.TX
  N3: Part1.D11_PWM/MOSI, R1.Pin_1
  N4: Part1.D2, R2.Pin_1
  N5: Part1.D3_PWM, R3.Pin_1
  N6: Part1.D4, R4.Pin_1
  N7: Part1.D5_PWM, R5.Pin_1
  N8: Part1.D6_PWM, HC-SR04_Sensor_1.ECHO
  N9: Part1.D7, HC-SR04_Sensor_1.TRIG
  VCC: Part1.5V, DFRobot_DFPlayer_Mini1.VCC, HC-SR04_Sensor_1.VCC
  GND: Part1.GND, DFRobot_DFPlayer_Mini1.GND-1, DFRobot_DFPlayer_Mini1.GND-2, HC-SR04_Sensor_1.GND, LED1.cathode, U1.S, U1.E, LED2.cathode, LED3.cathode, LED4.cathode
  N10: DFRobot_DFPlayer_Mini1.RX, R1.Pin_0
  N11: DFRobot_DFPlayer_Mini1.SPK_1, SP1.-
  N12: DFRobot_DFPlayer_Mini1.SPK_2, SP1.+
  N13: LED1.anode, R2.Pin_0
  N14: LED2.anode, R3.Pin_0
  N15: LED3.anode, R4.Pin_0
  N16: LED4.anode, R5.Pin_0
